// Logisim project smips.circ as structural Verilog: 9 circuits, main circuit Board
module Board (
);

  wire CLK, HALT, MEM_WE, RESET, TTY_WE;
  wire [3:0] MEM_BE;
  wire [6:0] TTY_DATA;
  wire [31:0] MEM_ADDR, MEM_RDATA, MEM_WDATA;

  Clock Reloj (.out(CLK));
  Button u_Reset (.out(RESET));
  CPU cpu_1 (
    .CLK(CLK), .RESET(RESET), .MEM_RDATA(MEM_RDATA), .MEM_ADDR(MEM_ADDR), .MEM_WDATA(MEM_WDATA),
    .MEM_BE(MEM_BE), .MEM_WE(MEM_WE), .TTY_DATA(TTY_DATA), .TTY_WE(TTY_WE), .HALT(HALT));
  TTY #(.cols(48), .rows(12)) tty_1 (.data(TTY_DATA), .clk(CLK), .we(TTY_WE), .clr(RESET));
  Memory memory_1 (.CLK(CLK), .ADDR(MEM_ADDR), .WDATA(MEM_WDATA), .BE(MEM_BE), .WE(MEM_WE), .RDATA(MEM_RDATA));
  LED u_Halt (.in(HALT));

  // Notes on the sheet:
  //   S-MIPS | Board
  //   No modificar: la CPU se implementa dentro del subcircuito CPU.
endmodule

module CPU (
  input  CLK,
  input  RESET,
  input  [31:0] MEM_RDATA,
  output [31:0] MEM_ADDR,
  output [31:0] MEM_WDATA,
  output [3:0] MEM_BE,
  output MEM_WE,
  output [6:0] TTY_DATA,
  output TTY_WE,
  output HALT
);

  wire ILLEGAL, IRWrite, Is_Beq, Is_Bne, Is_Branch, Is_Byte, Is_ImmALU, Is_Jal, Is_JR, Is_Jump, Is_LB_Signed,
       Is_Load, Is_Lui, Is_RType, Is_Shift, Is_Store, Is_Syscall;
  wire [1:0] ALUSrcA_SEL, ALUSrcB_SEL, IMM_MODE, PC_SEL;
  wire [2:0] ALU_OP, ALU_OP_DEC;
  wire [5:0] IR_Funct, IR_OP;

  Instruction_Decoder instruction_decoder_1 (
    .Funct(IR_Funct), .Op(IR_OP), .ALU_OP_DEC(ALU_OP_DEC), .Is_Syscall(Is_Syscall), .ILLEGAL(ILLEGAL),
    .Is_Jal(Is_Jal), .Is_Load(Is_Load), .Is_Beq(Is_Beq), .Is_Store(Is_Store), .Is_Bne(Is_Bne),
    .Is_Branch(Is_Branch), .Is_LB_Signed(Is_LB_Signed), .Is_Jump(Is_Jump), .Is_JR(Is_JR),
    .IMM_MODE(IMM_MODE), .Is_Lui(Is_Lui), .Is_Shift(Is_Shift), .Is_RType(Is_RType), .Is_Byte(Is_Byte),
    .Is_ImmALU(Is_ImmALU));
  Datapath datapath_1 (
    .CLK(CLK), .RESET(RESET), .ALUSrcA_SEL(ALUSrcA_SEL), .V0_SEL(Is_Syscall), .TTY_A0_SEL(Is_Syscall),
    .ALUSrcB_SEL(ALUSrcB_SEL), .IRWrite(IRWrite), .MEM_RDATA(MEM_RDATA), .ALU_OP(ALU_OP), .PC_SEL(PC_SEL),
    .L_SIGNED_SEL(Is_LB_Signed), .SB_SEL(Is_Byte), .IMM_MODE(IMM_MODE), .MEM_WDATA(MEM_RDATA),
    .IR_Funct(IR_Funct), .MEM_BE(MEM_BE), .IR_OP(IR_OP), .TTY_DATA(TTY_DATA));  // open: RegWrite, PCWrite, SB_EN, Wa_SEL, SW_EN, MEM_ADDR_SEL, WB_SEL, A_OUT, MEM_ADDR, B_OUT
  Control_Unit control_unit_1 (
    .CLK(CLK), .RESET(RESET), .ILLEGAL(ILLEGAL), .Is_Syscall(Is_Syscall), .Is_Load(Is_Load),
    .Is_Store(Is_Store), .Is_Branch(Is_Branch), .Is_Jump(Is_Jump), .Is_RType(Is_RType),
    .Is_ImmALU(Is_ImmALU), .Is_Shift(Is_Shift), .Is_Lui(Is_Lui), .Is_JR(Is_JR), .Is_JAL(Is_Jal),
    .Is_Beq(Is_Beq), .Is_Bne(Is_Bne), .Is_Byte(Is_Byte), .ALU_OP_DEC(ALU_OP_DEC), .ALUSrcA_SEL(ALUSrcA_SEL),
    .ALUSrcB_SEL(ALUSrcB_SEL), .ALU_OP(ALU_OP), .PC_SEL(PC_SEL), .IRWrite(IRWrite), .MEM_WE(MEM_WE),
    .TTY_WE(TTY_WE), .HALT(HALT));  // open: V0_IS_10, V0_IS_11, NEXT_STATE, PCWrite, MEM_ADDR_SEL, RegWrite, Wa_SEL, WB_SEL, SB_EN, SW_EN, Beq, Bne
  Branch_Control branch_control_1 ();  // open: Bne, Op1, Beq, PCWrite, Op2, PC_WE

  assign MEM_WDATA = MEM_RDATA;

  // Notes on the sheet:
  //   CPU S-MIPS: implementar aqui
  //   No cambiar nombres, anchos ni sentido de los pines: la placa depende de ellos.
endmodule

module Memory (
  input  CLK,
  input  [31:0] ADDR,
  input  [31:0] WDATA,
  input  [3:0] BE,
  input  WE,
  output [31:0] RDATA
);

  RAM #(.addrWidth(12), .asyncread("true"), .byteenables("byteEnables"), .dataWidth(32), .\type ("nonvolatile")) Main_Memory (
    .addr(ADDR[13:2]), .we(WE), .oe(1'b1), .clk(CLK), .din(WDATA), .dout(RDATA), .be3(BE[3]), .be2(BE[2]),
    .be1(BE[1]), .be0(BE[0]));

  // Other names for the same wires on the sheet: A[11:0] = ADDR[13:2]

  // Notes on the sheet:
  //   Memoria unificada: 4096 palabras de 32 bits (16 KiB), little-endian
  //   Lectura combinacional; escritura en el flanco de subida de CLK con WE=1, solo en los bytes con BE=1.
  //   Se usan los bits 13..2 de ADDR; los demas se ignoran (el espacio se repite cada 16 KiB).
endmodule

module Datapath (
  input  CLK,
  input  RESET,
  input  [1:0] ALUSrcA_SEL,
  input  V0_SEL,
  input  TTY_A0_SEL,
  input  [1:0] ALUSrcB_SEL,
  input  RegWrite,
  input  PCWrite,
  input  IRWrite,
  input  [31:0] MEM_RDATA,
  input  [2:0] ALU_OP,
  input  SB_EN,
  input  [1:0] Wa_SEL,
  input  SW_EN,
  input  [1:0] PC_SEL,
  input  MEM_ADDR_SEL,
  input  L_SIGNED_SEL,
  input  [1:0] WB_SEL,
  input  SB_SEL,
  input  [1:0] IMM_MODE,
  output [31:0] MEM_WDATA,
  output [5:0] IR_Funct,
  output [3:0] MEM_BE,
  output [31:0] A_OUT,
  output [31:0] MEM_ADDR,
  output [31:0] B_OUT,
  output [5:0] IR_OP,
  output [6:0] TTY_DATA
);

  wire and_5_out, and_6_out, and_7_out, and_8_out, sel_byte0, sel_byte1, sel_byte2, sel_byte3, V0_IS_10,
       V0_IS_11, ZERO;
  wire [4:0] multiplexer_2_out, multiplexer_3_out, RS, Wa_wr;
  wire [7:0] byte0O, byte1O, byte2O, byte3O, LOAD_BYTE;
  wire [15:6] Imm16;
  wire [25:16] IR_ADDR;
  wire [27:0] PC_OUT;
  wire [31:0] alu_1_result, ALUOUT, bit_extender_3_out, IMM_EXT, IMM_SGN, IMM_ZERO, LB, LB_EXT, LBU, MDROUT,
       multiplexer_10_out, multiplexer_11_out, multiplexer_14_out, RD1_O, RD2_O, shifter_1_out, undriven, WB;
  wire [31:28] JUMP_TARGET;

  Multiplexer #(.select(2), .width(32)) multiplexer_1 (
    .in0(ALUOUT), .in1(MDROUT), .in2(LB_EXT), .in3({JUMP_TARGET, PC_OUT}), .out(WB), .sel(WB_SEL));
  Multiplexer #(.width(5)) multiplexer_2 (.in0(RS), .in1(5'b00010), .out(multiplexer_2_out), .sel(V0_SEL));
  Multiplexer #(.width(5)) multiplexer_3 (
    .in0(IR_ADDR[20:16]), .in1(5'b00100), .out(multiplexer_3_out), .sel(TTY_A0_SEL));
  Multiplexer #(.select(2), .width(5)) multiplexer_4 (
    .in0(IR_ADDR[20:16]), .in1(Imm16[15:11]), .in2({5{1'b1}}), .in3({5{1'b0}}), .out(Wa_wr), .sel(Wa_SEL));
  Multiplexer #(.width(8)) multiplexer_5 (.in0({8{1'b0}}), .in1(B_OUT[7:0]), .out(byte0O), .sel(sel_byte0));
  Multiplexer #(.width(8)) multiplexer_6 (.in0({8{1'b0}}), .in1(B_OUT[7:0]), .out(byte1O), .sel(sel_byte1));
  Multiplexer #(.width(8)) multiplexer_7 (.in0({8{1'b0}}), .in1(B_OUT[7:0]), .out(byte2O), .sel(sel_byte2));
  Multiplexer #(.width(8)) multiplexer_8 (.in0({8{1'b0}}), .in1(B_OUT[7:0]), .out(byte3O), .sel(sel_byte3));
  Register_File register_file_1 (
    .CLK(CLK), .RESET(RESET), .RegWrite(RegWrite), .Rs(multiplexer_2_out), .Rt(multiplexer_3_out),
    .Wa_wr(Wa_wr), .Wd(WB), .READ_DATA1(RD1_O), .READ_DATA2(RD2_O));
  and and_1 (sel_byte0, ~MEM_ADDR[1], ~MEM_ADDR[0]);  // AND_Gate
  and and_2 (sel_byte1, ~MEM_ADDR[1], MEM_ADDR[0]);  // AND_Gate
  and and_3 (sel_byte2, MEM_ADDR[1], ~MEM_ADDR[0]);  // AND_Gate
  and and_4 (sel_byte3, MEM_ADDR[1], MEM_ADDR[0]);
  Register #(.width(32)) A (.D(RD1_O), .en(1'b1), .clk(CLK), .Q(A_OUT));  // open: clr
  Register #(.width(32)) B (.D(RD2_O), .en(1'b1), .clk(CLK), .Q(B_OUT));  // open: clr
  and and_5 (and_5_out, SB_EN, sel_byte0);
  and and_6 (and_6_out, SB_EN, sel_byte1);
  and and_7 (and_7_out, SB_EN, sel_byte2);
  and and_8 (and_8_out, SB_EN, sel_byte3);
  Multiplexer #(.width(32)) multiplexer_9 (
    .in0(B_OUT), .in1({byte3O, byte2O, byte1O, byte0O}), .out(MEM_WDATA), .sel(SB_SEL));
  assign IMM_ZERO = {{16{1'b0}}, {Imm16, IR_Funct}};  // Bit_Extender bit_extender_1
  assign IMM_SGN = {{16{Imm16[15]}}, {Imm16, IR_Funct}};  // Bit_Extender bit_extender_2
  or or_1 (MEM_BE[0], and_5_out, SW_EN);
  or or_2 (MEM_BE[1], and_6_out, SW_EN);
  or or_3 (MEM_BE[2], and_7_out, SW_EN);
  or or_4 (MEM_BE[3], and_8_out, SW_EN);
  assign bit_extender_3_out = {{27{1'b0}}, Imm16[10:6]};  // Bit_Extender bit_extender_3
  Shifter #(.width(32)) shifter_1 (.in(IMM_SGN), .\dist (5'b00010), .out(shifter_1_out));
  Multiplexer #(.select(2), .width(32)) multiplexer_10 (
    .in0({JUMP_TARGET, PC_OUT}), .in1(A_OUT), .in2(bit_extender_3_out), .in3({32{1'b0}}),
    .out(multiplexer_10_out), .sel(ALUSrcA_SEL));
  Multiplexer #(.select(2), .width(32)) multiplexer_11 (
    .in0(B_OUT), .in1(32'h4), .in2(IMM_EXT), .in3(shifter_1_out), .out(multiplexer_11_out), .sel(ALUSrcB_SEL));
  Bit_Extender #(.in_width(32), .out_width(7)) bit_extender_4 (.in(B_OUT), .out(TTY_DATA));
  Multiplexer #(.select(2), .width(32)) multiplexer_12 (
    .in0(IMM_SGN), .in1(IMM_ZERO), .in2({Imm16, IR_Funct, {16{1'b0}}}), .out(IMM_EXT), .sel(IMM_MODE));  // open: in3
  ALU alu_1 (.A(multiplexer_10_out), .B(multiplexer_11_out), .ALU_OP(ALU_OP), .RESULT(alu_1_result), .ZERO_F(ZERO));
  Register #(.width(32)) IR (
    .D(MEM_RDATA), .en(IRWrite), .clk(CLK), .Q({IR_OP, IR_ADDR, Imm16, IR_Funct}), .clr(RESET));
  Register #(.width(32)) MDR (.D(undriven), .clk(CLK), .Q(MDROUT));  // open: en, clr
  Multiplexer #(.select(2), .width(8)) multiplexer_13 (
    .in0(MEM_RDATA[7:0]), .in1(MEM_RDATA[15:8]), .in2(MEM_RDATA[23:16]), .in3(MEM_RDATA[31:24]),
    .out(LOAD_BYTE), .sel(MEM_ADDR[1:0]));
  Comparator #(.width(32)) comparator_1 (.a(A_OUT), .b(32'ha), .eq(V0_IS_10));  // open: gt, lt
  Comparator #(.width(32)) comparator_2 (.a(A_OUT), .b(32'hb), .eq(V0_IS_11));  // open: gt, lt
  Register #(.width(32)) u_ALUOUT (.D(alu_1_result), .clk(CLK), .Q(ALUOUT));  // open: en, clr
  assign LB = {{24{LOAD_BYTE[7]}}, LOAD_BYTE};  // Bit_Extender bit_extender_5
  assign LBU = {{24{1'b0}}, LOAD_BYTE};  // Bit_Extender bit_extender_6
  Register #(.width(32)) PC (.D(multiplexer_14_out), .en(PCWrite), .clk(CLK), .Q({JUMP_TARGET, PC_OUT}), .clr(RESET));
  Multiplexer #(.select(2), .width(32)) multiplexer_14 (
    .in0(ALUOUT), .in1({JUMP_TARGET, IR_ADDR, Imm16, IR_Funct, 2'b00}), .in2(A_OUT),
    .out(multiplexer_14_out), .sel(PC_SEL));  // open: in3
  Multiplexer #(.width(32)) multiplexer_15 (
    .in0(ALUOUT), .in1({JUMP_TARGET, PC_OUT}), .out(MEM_ADDR), .sel(MEM_ADDR_SEL));
  Multiplexer #(.width(32)) multiplexer_16 (.in0(LBU), .in1(LB), .out(LB_EXT), .sel(L_SIGNED_SEL));

  // Other names for the same wires on the sheet: A_O[31:0] = A_OUT; B_O[31:0] = B_OUT; byte0[7:0] = B_OUT[7:0];
  //   Imm16[5:0] = IR_Funct; IMM_LUI[31:16] = {Imm16, IR_Funct}; IR_ADDR[15:0] = {Imm16, IR_Funct};
  //   IR_OUT[31:0] = {IR_OP, IR_ADDR, Imm16, IR_Funct}; JUMP_TARGET[27:2] = {IR_ADDR, Imm16, IR_Funct};
  //   Shamt[4:0] = Imm16[10:6]; Rd[4:0] = Imm16[15:11]; Rt[4:0] = IR_ADDR[20:16]; Rs_t[4:0] = IR_ADDR[25:21];
  //   A0 = MEM_ADDR[0]; LB_SEL[1:0] = MEM_ADDR[1:0]; A1 = MEM_ADDR[1]; MEM_BYTE0[7:0] = MEM_RDATA[7:0];
  //   MEM_BYTE1[7:0] = MEM_RDATA[15:8]; MEM_BYTE2[7:0] = MEM_RDATA[23:16]; MEM_BYTE3[7:0] = MEM_RDATA[31:24];
  //   PC_HIGH[3:0] = JUMP_TARGET; PC_OUT[31:28] = JUMP_TARGET; SB_ALIGNED[31:0] = {byte3O, byte2O, byte1O, byte0O}

  // Notes on the sheet:
  //   LOGIC
  //   WRITE RF
  //   JUMP TARGET
  //   INPUTS
  //   SB
  //   Wa_wr
  //   REGISTER FILE LOGIC
  //   OUTPUTS
  //   IMM MODE
  //   MEM_BE
  //   ALUSrcA
  //   ALUSrcB
  //   TTY_DATA
  //   ALU LOGIC
  //   MDR
  //   LB / LW
  //   INST_REGISTER
  //   MEM_ADDR
  //   PC
endmodule

module Control_Unit (
  input  CLK,
  input  RESET,
  input  ILLEGAL,
  input  Is_Syscall,
  input  Is_Load,
  input  Is_Store,
  input  Is_Branch,
  input  Is_Jump,
  input  Is_RType,
  input  Is_ImmALU,
  input  Is_Shift,
  input  Is_Lui,
  input  Is_JR,
  input  Is_JAL,
  input  Is_Beq,
  input  Is_Bne,
  input  Is_Byte,
  input  [2:0] ALU_OP_DEC,
  input  V0_IS_10,
  input  V0_IS_11,
  input  [3:0] NEXT_STATE,
  output [1:0] ALUSrcA_SEL,
  output [1:0] ALUSrcB_SEL,
  output [2:0] ALU_OP,
  output [1:0] PC_SEL,
  output PCWrite,
  output IRWrite,
  output MEM_ADDR_SEL,
  output RegWrite,
  output [1:0] Wa_SEL,
  output [1:0] WB_SEL,
  output SB_EN,
  output SW_EN,
  output MEM_WE,
  output TTY_WE,
  output HALT,
  output Beq,
  output Bne
);

  wire a0, a1, AS1, b0, b1, b2, c0, c1, d0, D_B1, D_B2, D_B3, e0, f0, g0, h0, h1, MEMOPS, N0, N_ILLEGAL,
       N_Is_Byte, N_Is_Load, N_Is_RType, N_Is_Shift, N_V0_IS_10, S_BR_COMMIT, S_BR_TGT, S_DECODE, S_EXEC,
       S_MEMADR, S_MEMRD, S_SYS, S_WB_ALU, S_WB_LOAD, V_ANY;
  wire [3:0] STATE;

  and and_1 (ALUSrcA_SEL[1], S_EXEC, AS1);
  and and_2 (e0, S_EXEC, N_Is_Shift);
  or or_1 (ALUSrcA_SEL[0], e0, MEMOPS);
  and and_3 (f0, S_EXEC, N_Is_RType);
  or or_2 (ALUSrcB_SEL[0], f0, MEMOPS, S_BR_TGT);
  or or_3 (ALUSrcB_SEL[1], IRWrite, S_BR_TGT);
  and and_4 (g0, S_DECODE, N_ILLEGAL);
  or or_4 (PCWrite, g0, PC_SEL[0], PC_SEL[1]);
  or or_5 (RegWrite, S_WB_ALU, S_WB_LOAD, Wa_SEL[1]);
  and and_5 (Wa_SEL[0], S_WB_ALU, Is_RType);
  and and_6 (h0, S_WB_LOAD, Is_Byte);
  or or_6 (WB_SEL[1], h0, Wa_SEL[1]);
  and and_7 (h1, S_WB_LOAD, N_Is_Byte);
  or or_7 (WB_SEL[0], h1, Wa_SEL[1]);
  and and_8 (SB_EN, MEM_WE, Is_Byte);
  and and_9 (SW_EN, MEM_WE, N_Is_Byte);
  and and_10 (Beq, S_BR_COMMIT, Is_Beq);
  and and_11 (Bne, S_BR_COMMIT, Is_Bne);
  not not_1 (N_ILLEGAL, ILLEGAL);
  not not_2 (N_Is_Load, Is_Load);
  not not_3 (N_Is_Shift, Is_Shift);
  not not_4 (N_Is_RType, Is_RType);
  not not_5 (N_Is_Byte, Is_Byte);
  not not_6 (N_V0_IS_10, V0_IS_10);
  Register #(.width(4)) u_STATE (.D(NEXT_STATE), .clk(CLK), .Q(STATE), .clr(RESET));  // open: en
  Multiplexer #(.width(3)) multiplexer_1 (.in0(3'b000), .in1(ALU_OP_DEC), .out(ALU_OP), .sel(S_EXEC));
  Decoder #(.enable("false"), .select(4)) decoder_1 (
    .out0(IRWrite), .out1(S_DECODE), .out2(S_EXEC), .out3(S_WB_ALU), .out4(S_MEMADR), .out5(S_MEMRD),
    .out6(S_WB_LOAD), .out7(MEM_WE), .out8(S_BR_TGT), .out9(S_BR_COMMIT), .out10(PC_SEL[0]),
    .out11(PC_SEL[1]), .out12(S_SYS), .out13(TTY_WE), .out14(HALT), .sel(STATE));  // open: out15
  and and_12 (a0, S_DECODE, Is_JR);
  and and_13 (a1, S_SYS, N_V0_IS_10, V0_IS_11);
  and and_14 (b0, S_DECODE, D_B1);
  and and_15 (b1, S_MEMADR, N_Is_Load);
  and and_16 (b2, S_SYS, V0_IS_10);
  and and_17 (c0, S_DECODE, D_B2);
  or or_8 (AS1, Is_Shift, Is_Lui);
  or or_9 (MEMOPS, S_MEMADR, S_MEMRD, S_WB_LOAD, MEM_WE);
  or or_10 (V_ANY, V0_IS_10, V0_IS_11);
  or or_11 (D_B1, ILLEGAL, Is_RType, Is_ImmALU, Is_Jump, Is_JR);
  and and_18 (c1, S_SYS, V_ANY);
  and and_19 (d0, S_DECODE, D_B3);
  or or_12 (N0, IRWrite, a0, S_EXEC, S_MEMADR, S_BR_TGT, a1);
  or or_13 (NEXT_STATE[0], b0, S_EXEC, b1, S_MEMRD, b2, HALT);
  or or_14 (D_B2, ILLEGAL, Is_Syscall, Is_Load, Is_Store);
  or or_15 (D_B3, ILLEGAL, Is_Syscall, Is_Branch, Is_Jump, Is_JR);
  and and_20 (Wa_SEL[1], PC_SEL[0], Is_JAL);
  or or_16 (NEXT_STATE[1], c0, S_MEMADR, S_MEMRD, c1, HALT);
  or or_17 (NEXT_STATE[2], d0, S_BR_TGT, c1, HALT);

  assign MEM_ADDR_SEL = IRWrite;

  // Other names for the same wires on the sheet: ASA0 = ALUSrcA_SEL[0]; ASA1 = ALUSrcA_SEL[1]; ASB1 = ALUSrcB_SEL[0];
  //   ASB0 = ALUSrcB_SEL[1]; N1 = NEXT_STATE[0]; N2 = NEXT_STATE[1]; N3 = NEXT_STATE[2]; N4 = NEXT_STATE[3];
  //   S_JUMP = PC_SEL[0]; S_JR = PC_SEL[1]; S_FETCH = IRWrite; S_HALT = HALT; S_MEMWR = MEM_WE; S_PRINT = TTY_WE;
  //   WA0 = Wa_SEL[0]; JAL_NOW = Wa_SEL[1]; WBS0 = WB_SEL[0]; WBS1 = WB_SEL[1]

  // Notes on the sheet:
  //   INPUTS
  //   SALIDAS
  //   OUTPUTS
  //   NOT
  //   DECODER
  //   NEXT STATE
  //   AUXILIARS
endmodule

module Instruction_Decoder (
  input  [5:0] Funct,
  input  [5:0] Op,
  output [2:0] ALU_OP_DEC,
  output Is_Syscall,
  output ILLEGAL,
  output Is_Jal,
  output Is_Load,
  output Is_Beq,
  output Is_Store,
  output Is_Bne,
  output Is_Branch,
  output Is_LB_Signed,
  output Is_Jump,
  output Is_JR,
  output [1:0] IMM_MODE,
  output Is_Lui,
  output Is_Shift,
  output Is_RType,
  output Is_Byte,
  output Is_ImmALU
);

  wire comparator_1_eq, comparator_2_eq, comparator_5_eq, comparator_9_eq, comparator_11_eq,
       comparator_12_eq, comparator_14_eq, comparator_15_eq, comparator_16_eq, comparator_17_eq,
       comparator_18_eq, comparator_19_eq, comparator_21_eq, comparator_22_eq, comparator_25_eq, I_ADD,
       I_AND, I_OR, I_SLT, I_VALID, OP_LBU, OP_SB, OP_ZERO, or_5_out, R_ADD, R_AND, R_OR, R_SLL, R_SLT,
       R_SRL, R_SUB, R_VALID, VALID_INS;

  Comparator #(.width(6)) comparator_1 (.a(Funct), .b(6'b001100), .eq(comparator_1_eq));  // open: gt, lt
  Comparator #(.width(6)) comparator_2 (.a(Op), .b(6'b100011), .eq(comparator_2_eq));  // open: gt, lt
  Comparator #(.width(6)) comparator_3 (.a(Op), .b(6'b100000), .eq(Is_LB_Signed));  // open: gt, lt
  Comparator #(.width(6)) comparator_4 (.a(Op), .b(6'b100100), .eq(OP_LBU));  // open: gt, lt
  Comparator #(.width(6)) comparator_5 (.a(Op), .b(6'b101011), .eq(comparator_5_eq));  // open: gt, lt
  Comparator #(.width(6)) comparator_6 (.a(Op), .b(6'b101000), .eq(OP_SB));  // open: gt, lt
  Comparator #(.width(6)) comparator_7 (.a(Op), .b(6'b000100), .eq(Is_Beq));  // open: gt, lt
  Comparator #(.width(6)) comparator_8 (.a(Op), .b(6'b000101), .eq(Is_Bne));  // open: gt, lt
  Comparator #(.width(6)) comparator_9 (.a(Op), .b(6'b000010), .eq(comparator_9_eq));  // open: gt, lt
  Comparator #(.width(6)) comparator_10 (.a(Op), .b(6'b000011), .eq(Is_Jal));  // open: gt, lt
  and and_1 (Is_Syscall, comparator_1_eq, OP_ZERO);
  or or_1 (Is_Store, comparator_5_eq, OP_SB);
  or or_2 (Is_Branch, Is_Beq, Is_Bne);
  or or_3 (Is_Jump, comparator_9_eq, Is_Jal);
  nor nor_1 (OP_ZERO, Op[0], Op[1], Op[2], Op[3], Op[4], Op[5]);
  or or_4 (Is_Load, comparator_2_eq, Is_LB_Signed, OP_LBU);
  Comparator #(.width(6)) comparator_11 (.a(Funct), .b(6'b100000), .eq(comparator_11_eq));  // open: gt, lt
  Comparator #(.width(6)) comparator_12 (.a(Funct), .b(6'b100001), .eq(comparator_12_eq));  // open: gt, lt
  Comparator #(.width(6)) comparator_13 (.a(Op), .b(6'b001100), .eq(I_AND));  // open: gt, lt
  Comparator #(.width(6)) comparator_14 (.a(Funct), .b(6'b100010), .eq(comparator_14_eq));  // open: gt, lt
  Comparator #(.width(6)) comparator_15 (.a(Funct), .b(6'b100100), .eq(comparator_15_eq));  // open: gt, lt
  Comparator #(.width(6)) comparator_16 (.a(Funct), .b(6'b100101), .eq(comparator_16_eq));  // open: gt, lt
  Comparator #(.width(6)) comparator_17 (.a(Funct), .b(6'b101010), .eq(comparator_17_eq));  // open: gt, lt
  Comparator #(.width(6)) comparator_18 (.a(Funct), .b({6{1'b0}}), .eq(comparator_18_eq));  // open: gt, lt
  Comparator #(.width(6)) comparator_19 (.a(Funct), .b(6'b000010), .eq(comparator_19_eq));  // open: gt, lt
  or or_5 (or_5_out, comparator_11_eq, comparator_12_eq);
  and and_2 (R_SUB, comparator_14_eq, OP_ZERO);
  and and_3 (R_AND, comparator_15_eq, OP_ZERO);
  and and_4 (R_OR, comparator_16_eq, OP_ZERO);
  and and_5 (R_SLT, comparator_17_eq, OP_ZERO);
  and and_6 (R_SLL, comparator_18_eq, OP_ZERO);
  and and_7 (R_SRL, comparator_19_eq, OP_ZERO);
  or or_6 (IMM_MODE[0], I_OR, I_AND);
  and and_8 (R_ADD, or_5_out, OP_ZERO);
  Comparator #(.width(6)) comparator_20 (.a(Op), .b(6'b001101), .eq(I_OR));  // open: gt, lt
  Comparator #(.width(6)) comparator_21 (.a(Op), .b(6'b001000), .eq(comparator_21_eq));  // open: gt, lt
  Comparator #(.width(6)) comparator_22 (.a(Op), .b(6'b001001), .eq(comparator_22_eq));  // open: gt, lt
  Comparator #(.width(6)) comparator_23 (.a(Op), .b(6'b001010), .eq(I_SLT));  // open: gt, lt
  or or_7 (ALU_OP_DEC[0], I_OR, R_OR, R_SUB, Is_Branch, R_SLL);
  or or_8 (ALU_OP_DEC[1], R_AND, R_OR, I_AND, I_OR, R_SRL);
  or or_9 (ALU_OP_DEC[2], I_SLT, R_SRL, R_SLT, R_SLL);
  or or_10 (I_ADD, comparator_21_eq, comparator_22_eq);
  Comparator #(.width(6)) comparator_24 (.a(Op), .b(6'b001111), .eq(IMM_MODE[1]));  // open: gt, lt
  Comparator #(.width(6)) comparator_25 (.a(Funct), .b(6'b001000), .eq(comparator_25_eq));  // open: gt, lt
  or or_11 (R_VALID, R_SRL, R_SLL, R_SLT, R_SUB, R_OR, Is_JR, R_AND, R_ADD);
  or or_12 (I_VALID, Is_Store, Is_Load, I_SLT, I_OR, IMM_MODE[1], I_AND, I_ADD);
  and and_9 (Is_JR, comparator_25_eq, OP_ZERO);
  or or_13 (VALID_INS, Is_Syscall, R_VALID, I_VALID, Is_Branch, Is_Jump);
  not not_1 (ILLEGAL, VALID_INS);
  or or_14 (Is_Shift, R_SLL, R_SRL);
  or or_15 (Is_Byte, Is_LB_Signed, OP_LBU, OP_SB);
  or or_16 (Is_ImmALU, I_ADD, I_AND, I_OR, I_SLT, IMM_MODE[1]);
  or or_17 (Is_RType, R_ADD, R_SUB, R_AND, R_OR, R_SLT, R_SLL, R_SRL);

  assign Is_Lui = IMM_MODE[1];

  // Other names for the same wires on the sheet: ALU_OP_0 = ALU_OP_DEC[0]; ALU_OP_1 = ALU_OP_DEC[1];
  //   ALU_OP_2 = ALU_OP_DEC[2]; IMM_ZERO = IMM_MODE[0]; I_LUI = IMM_MODE[1]; IMM_LUI = IMM_MODE[1]; OP_BEQ = Is_Beq;
  //   OP_BNE = Is_Bne; OP_JAL = Is_Jal; OP_LB = Is_LB_Signed; R_JR = Is_JR

  // Notes on the sheet:
  //   INPUTS
  //   IS SHIFT
  //   IS BYTE
  //   Is-RType
  //   Is_ImmALU
  //   OUTPUTS
endmodule

module Branch_Control (
  input  Bne,
  input  [31:0] Op1,
  input  Beq,
  input  PCWrite,
  input  [31:0] Op2,
  output PC_WE
);

  wire and_1_out, and_2_out, comparator_1_eq, not_1_out, or_1_out;

  Comparator #(.width(32)) comparator_1 (.a(Op1), .b(Op2), .eq(comparator_1_eq));  // open: gt, lt
  not not_1 (not_1_out, comparator_1_eq);
  and and_1 (and_1_out, comparator_1_eq, Beq);
  and and_2 (and_2_out, Bne, not_1_out);
  or or_1 (or_1_out, and_2_out, and_1_out);
  or or_2 (PC_WE, or_1_out, PCWrite);
endmodule

module Register_File (
  input  CLK,
  input  RESET,
  input  RegWrite,
  input  [4:0] Rs,
  input  [4:0] Rt,
  input  [4:0] Wa_wr,
  input  [31:0] Wd,
  output [31:0] READ_DATA1,
  output [31:0] READ_DATA2
);

  wire decoder_1_out1, decoder_1_out2, decoder_1_out3, decoder_1_out4, decoder_1_out5, decoder_1_out6,
       decoder_1_out7, decoder_1_out8, decoder_1_out9, decoder_1_out10, decoder_1_out11, decoder_1_out12,
       decoder_1_out13, decoder_1_out14, decoder_1_out15, decoder_1_out16, decoder_1_out17, decoder_1_out18,
       decoder_1_out19, decoder_1_out20, decoder_1_out21, decoder_1_out22, decoder_1_out23, decoder_1_out24,
       decoder_1_out25, decoder_1_out26, decoder_1_out27, decoder_1_out28, decoder_1_out29, decoder_1_out30,
       decoder_1_out31, R0, R1, R2, R3, R4, R5, R6, R7, R8, R9, R10, R11, R12, R13, R14, R15, R16, R17, R18,
       R19, R20, R21, R22, R23, R24, R25, R26, R27, R28, R28E, R29, R29E, R30, R31;
  wire [31:0] R0O, R1O, R2O, R3O, R4O, R5O, R6O, R7O, R8O, R9O, R10O, R11O, R12O, R13O, R14O, R15O, R16O,
       R17O, R18O, R19O, R20O, R21O, R22O, R23O, R24O, R25O, R26O, R27O, R28_D, R28O, R29_D, R29O, R30O, R31O;

  Register #(.width(32)) u_R0 (.D(Wd), .en(R0), .clk(CLK), .Q(R0O), .clr(RESET));
  Register #(.width(32)) u_R4 (.D(Wd), .en(R4), .clk(CLK), .Q(R4O), .clr(RESET));
  Register #(.width(32)) u_R8 (.D(Wd), .en(R8), .clk(CLK), .Q(R8O), .clr(RESET));
  Register #(.width(32)) u_R12 (.D(Wd), .en(R12), .clk(CLK), .Q(R12O), .clr(RESET));
  Register #(.width(32)) u_R16 (.D(Wd), .en(R16), .clk(CLK), .Q(R16O), .clr(RESET));
  Register #(.width(32)) u_R20 (.D(Wd), .en(R20), .clk(CLK), .Q(R20O), .clr(RESET));
  Register #(.width(32)) u_R24 (.D(Wd), .en(R24), .clk(CLK), .Q(R24O), .clr(RESET));
  Register #(.width(32)) u_R28 (.D(R28_D), .en(R28E), .clk(CLK), .Q(R28O), .clr(1'b0));
  Multiplexer #(.width(32)) multiplexer_1 (.in0(Wd), .in1(32'h1800), .out(R28_D), .sel(RESET));
  Register #(.width(32)) u_R1 (.D(Wd), .en(R1), .clk(CLK), .Q(R1O), .clr(RESET));
  Register #(.width(32)) u_R5 (.D(Wd), .en(R5), .clk(CLK), .Q(R5O), .clr(RESET));
  Register #(.width(32)) u_R9 (.D(Wd), .en(R9), .clk(CLK), .Q(R9O), .clr(RESET));
  Register #(.width(32)) u_R13 (.D(Wd), .en(R13), .clk(CLK), .Q(R13O), .clr(RESET));
  Register #(.width(32)) u_R17 (.D(Wd), .en(R17), .clk(CLK), .Q(R17O), .clr(RESET));
  Register #(.width(32)) u_R21 (.D(Wd), .en(R21), .clk(CLK), .Q(R21O), .clr(RESET));
  Register #(.width(32)) u_R25 (.D(Wd), .en(R25), .clk(CLK), .Q(R25O), .clr(RESET));
  Register #(.width(32)) u_R29 (.D(R29_D), .en(R29E), .clk(CLK), .Q(R29O), .clr(1'b0));
  or or_1 (R28E, R28, RESET);
  Register #(.width(32)) u_R2 (.D(Wd), .en(R2), .clk(CLK), .Q(R2O), .clr(RESET));
  Register #(.width(32)) u_R6 (.D(Wd), .en(R6), .clk(CLK), .Q(R6O), .clr(RESET));
  Register #(.width(32)) u_R10 (.D(Wd), .en(R10), .clk(CLK), .Q(R10O), .clr(RESET));
  Register #(.width(32)) u_R14 (.D(Wd), .en(R14), .clk(CLK), .Q(R14O), .clr(RESET));
  Register #(.width(32)) u_R18 (.D(Wd), .en(R18), .clk(CLK), .Q(R18O), .clr(RESET));
  Register #(.width(32)) u_R22 (.D(Wd), .en(R22), .clk(CLK), .Q(R22O), .clr(RESET));
  Register #(.width(32)) u_R26 (.D(Wd), .en(R26), .clk(CLK), .Q(R26O), .clr(RESET));
  Register #(.width(32)) u_R30 (.D(Wd), .en(R30), .clk(CLK), .Q(R30O), .clr(RESET));
  Multiplexer #(.width(32)) multiplexer_2 (.in0(Wd), .in1(32'h3ffc), .out(R29_D), .sel(RESET));
  Register #(.width(32)) u_R3 (.D(Wd), .en(R3), .clk(CLK), .Q(R3O), .clr(RESET));
  Register #(.width(32)) u_R7 (.D(Wd), .en(R7), .clk(CLK), .Q(R7O), .clr(RESET));
  Register #(.width(32)) u_R11 (.D(Wd), .en(R11), .clk(CLK), .Q(R11O), .clr(RESET));
  Register #(.width(32)) u_R15 (.D(Wd), .en(R15), .clk(CLK), .Q(R15O), .clr(RESET));
  Register #(.width(32)) u_R19 (.D(Wd), .en(R19), .clk(CLK), .Q(R19O), .clr(RESET));
  Register #(.width(32)) u_R23 (.D(Wd), .en(R23), .clk(CLK), .Q(R23O), .clr(RESET));
  Register #(.width(32)) u_R27 (.D(Wd), .en(R27), .clk(CLK), .Q(R27O), .clr(RESET));
  Register #(.width(32)) u_R31 (.D(Wd), .en(R31), .clk(CLK), .Q(R31O), .clr(RESET));
  or or_2 (R29E, R29, RESET);
  Decoder #(.select(5)) decoder_1 (
    .out1(decoder_1_out1), .out2(decoder_1_out2), .out3(decoder_1_out3), .out4(decoder_1_out4),
    .out5(decoder_1_out5), .out6(decoder_1_out6), .out7(decoder_1_out7), .out8(decoder_1_out8),
    .out9(decoder_1_out9), .out10(decoder_1_out10), .out11(decoder_1_out11), .out12(decoder_1_out12),
    .out13(decoder_1_out13), .out14(decoder_1_out14), .out15(decoder_1_out15), .out16(decoder_1_out16),
    .out17(decoder_1_out17), .out18(decoder_1_out18), .out19(decoder_1_out19), .out20(decoder_1_out20),
    .out21(decoder_1_out21), .out22(decoder_1_out22), .out23(decoder_1_out23), .out24(decoder_1_out24),
    .out25(decoder_1_out25), .out26(decoder_1_out26), .out27(decoder_1_out27), .out28(decoder_1_out28),
    .out29(decoder_1_out29), .out30(decoder_1_out30), .out31(decoder_1_out31), .sel(Wa_wr));  // open: out0, en
  and and_1 (R0, RegWrite, 1'b0);
  and and_2 (R1, RegWrite, decoder_1_out1);
  and and_3 (R31, RegWrite, decoder_1_out31);
  and and_4 (R30, RegWrite, decoder_1_out30);
  and and_5 (R2, RegWrite, decoder_1_out2);
  and and_6 (R3, RegWrite, decoder_1_out3);
  and and_7 (R29, RegWrite, decoder_1_out29);
  and and_8 (R28, RegWrite, decoder_1_out28);
  and and_9 (R4, RegWrite, decoder_1_out4);
  and and_10 (R5, RegWrite, decoder_1_out5);
  and and_11 (R27, RegWrite, decoder_1_out27);
  and and_12 (R26, RegWrite, decoder_1_out26);
  and and_13 (R6, RegWrite, decoder_1_out6);
  and and_14 (R7, RegWrite, decoder_1_out7);
  and and_15 (R25, RegWrite, decoder_1_out25);
  and and_16 (R24, RegWrite, decoder_1_out24);
  Multiplexer #(.select(5), .width(32)) multiplexer_3 (
    .in0(R0O), .in1(R1O), .in2(R2O), .in3(R3O), .in4(R4O), .in5(R5O), .in6(R6O), .in7(R7O), .in8(R8O),
    .in9(R9O), .in10(R10O), .in11(R11O), .in12(R12O), .in13(R13O), .in14(R14O), .in15(R15O), .in16(R16O),
    .in17(R17O), .in18(R18O), .in19(R19O), .in20(R20O), .in21(R21O), .in22(R22O), .in23(R23O), .in24(R24O),
    .in25(R25O), .in26(R26O), .in27(R27O), .in28(R28O), .in29(R29O), .in30(R30O), .in31(R31O),
    .out(READ_DATA1), .sel(Rs));
  Multiplexer #(.select(5), .width(32)) multiplexer_4 (
    .in0(R0O), .in1(R1O), .in2(R2O), .in3(R3O), .in4(R4O), .in5(R5O), .in6(R6O), .in7(R7O), .in8(R8O),
    .in9(R9O), .in10(R10O), .in11(R11O), .in12(R12O), .in13(R13O), .in14(R14O), .in15(R15O), .in16(R16O),
    .in17(R17O), .in18(R18O), .in19(R19O), .in20(R20O), .in21(R21O), .in22(R22O), .in23(R23O), .in24(R24O),
    .in25(R25O), .in26(R26O), .in27(R27O), .in28(R28O), .in29(R29O), .in30(R30O), .in31(R31O),
    .out(READ_DATA2), .sel(Rt));
  and and_17 (R8, RegWrite, decoder_1_out8);
  and and_18 (R9, RegWrite, decoder_1_out9);
  and and_19 (R23, RegWrite, decoder_1_out23);
  and and_20 (R22, RegWrite, decoder_1_out22);
  and and_21 (R10, RegWrite, decoder_1_out10);
  and and_22 (R11, RegWrite, decoder_1_out11);
  and and_23 (R21, RegWrite, decoder_1_out21);
  and and_24 (R20, RegWrite, decoder_1_out20);
  and and_25 (R12, RegWrite, decoder_1_out12);
  and and_26 (R13, RegWrite, decoder_1_out13);
  and and_27 (R19, RegWrite, decoder_1_out19);
  and and_28 (R18, RegWrite, decoder_1_out18);
  and and_29 (R14, RegWrite, decoder_1_out14);
  and and_30 (R15, RegWrite, decoder_1_out15);
  and and_31 (R17, RegWrite, decoder_1_out17);
  and and_32 (R16, RegWrite, decoder_1_out16);

  // Notes on the sheet:
  //   INPUTS
  //   OUTPUTS
  //   R28
  //   REGISTER_BANK
  //   R29
  //   REGISTER SELECTOR
  //   OUTPUT SELECTOR
endmodule

module ALU (
  input  [31:0] A,
  input  [31:0] B,
  input  [2:0] ALU_OP,
  output [31:0] RESULT,
  output ZERO_F
);

  wire comparator_1_lt;
  wire [31:0] ADD, ALU_AND, ALU_OR, L_LEFT, L_RIGHT, SLT, SUB;

  assign ALU_AND = A & B;  // AND_Gate and_1, 32 bits wide
  Shifter #(.width(32)) shifter_1 (.in(B), .\dist (A[4:0]), .out(L_LEFT));
  Adder #(.width(32)) adder_1 (.a(A), .b(B), .out(ADD));  // open: cin, cout
  Comparator #(.width(32)) comparator_1 (.a(A), .b(B), .lt(comparator_1_lt));  // open: gt, eq
  assign SLT = {{31{1'b0}}, comparator_1_lt};  // Bit_Extender bit_extender_1
  Subtractor #(.width(32)) subtractor_1 (.a(A), .b(B), .out(SUB));  // open: bin, bout
  assign ALU_OR = A | B;  // OR_Gate or_1, 32 bits wide
  Shifter #(.shift("lr"), .width(32)) shifter_2 (.in(B), .\dist (A[4:0]), .out(L_RIGHT));
  Multiplexer #(.select(3), .width(32)) multiplexer_1 (
    .in0(ADD), .in1(SUB), .in2(ALU_AND), .in3(ALU_OR), .in4(SLT), .in5(L_LEFT), .in6(L_RIGHT), .in7(B),
    .out(RESULT), .sel(ALU_OP));
  Comparator #(.width(32)) comparator_2 (.a({32{1'b0}}), .b(RESULT), .eq(ZERO_F));  // open: gt, lt

  // Other names for the same wires on the sheet: ZERO = ZERO_F

  // Notes on the sheet:
  //   INPUTS
  //   OPERATIONS
  //   OUTPUTS
  //   CODIFICATIONS
  //   000  ADD
  //   001 SUB
  //   010 AND
  //   011 OR
  //   100 SLT
  //   101 SLL
  //   110 SRL
  //   LOGIC
endmodule
